// Logisim project LC3-2200a.circ as structural Verilog: 6 circuits, main circuit my circuit
module my_circuit (
  output [31:0] out_1,
  output [3:0] out_2,
  output [31:0] out_3,
  output [31:0] out_4,
  output [31:0] out_5,
  output [31:0] out_6,
  output [31:0] out_7,
  output [31:0] out_8,
  output [31:0] out_9,
  output [31:0] out_10,
  output [1:0] out_11,
  output [1:0] out_12,
  output [31:0] out_13,
  output [3:0] out_14,
  output [31:0] out_15,
  output [31:0] out_16,
  output [31:0] out_17,
  output [31:0] out_18,
  output [2:0] out_19,
  output [31:0] out_20,
  output [2:0] out_21,
  output [31:0] out_22,
  output [31:0] out_23,
  output [31:0] out_24
);

  wire CheckCC, clock, DrALU, DrMem, DrOff, DrPC, DrReg, LdA, LdB, LdCC, LdIR, LdMar, LdPC, not_1_out, WrMem,
       WrtReg;
  wire [2:0] comparator_1_gt;
  wire [7:0] register_5_q_2;
  wire [23:0] register_5_q;
  wire [31:0] fp, ram_1_data, register_1_q, registerfile_1_output, sp;

  Clock clock_1 (.out(clock));
  Register #(.width(32)) register_1 (.D(out_16), .en(LdPC), .Q(register_1_q), .clk(clock));  // open: clr
  assign out_16 = DrPC ? register_1_q : 32'bz;  // Controlled_Buffer controlled_buffer_1
  Register #(.width(32)) register_2 (.D(out_16), .en(LdA), .Q(out_15), .clk(clock));  // open: clr
  ALU alu_1 (.A(out_15), .B(out_20), .Output(out_7), .control(out_11));
  Comparator #(.width(32)) comparator_1 (
    .a(out_16), .b({32{1'b0}}), .gt(comparator_1_gt[0]), .eq(comparator_1_gt[1]), .lt(comparator_1_gt[2]));
  assign out_16 = DrALU ? out_7 : 32'bz;  // Controlled_Buffer controlled_buffer_2
  Register #(.width(32)) register_3 (.D(out_16), .en(LdB), .Q(out_20), .clk(clock));  // open: clr
  assign out_16 = DrReg ? registerfile_1_output : 32'bz;  // Controlled_Buffer controlled_buffer_3
  RegisterFile registerfile_1 (
    .Din(out_16), .clk(clock), .Regno(out_14), .WrtReg(WrtReg), .\output (registerfile_1_output), .v0(out_3),
    .a0(out_4), .t0(out_8), .t1(out_10), .t2(out_13), .s0(out_18), .fp(fp), .at(out_17), .a1(out_5),
    .k0(out_22), .a2(out_6), .s1(out_23), .s2(out_24), .s_prime_p(sp));
  Register #(.width(3)) register_4 (.D(comparator_1_gt), .en(LdCC), .Q(out_21), .clk(clock));  // open: clr
  QieKCC qiekcc_1 (.in_1(out_1[22:20]), .in_2(out_21), .\output (CheckCC));
  Register #(.width(32)) register_5 (
    .D(out_16), .en(LdMar), .Q({register_5_q_2, register_5_q}), .clk(clock));  // open: clr
  RAM #(.addrWidth(24), .dataWidth(32), .bus("separate")) ram_1 (
    .addr(register_5_q), .din(out_16), .data(ram_1_data), .str(WrMem), .clk(clock), .ld(not_1_out));  // open: sel, clr
  not not_1 (not_1_out, WrMem);
  assign out_16 = DrMem ? ram_1_data : 32'bz;  // Controlled_Buffer controlled_buffer_4
  Register #(.width(32)) IR (.D(out_16), .en(LdIR), .Q(out_1), .clk(clock));  // open: clr
  assign out_9 = {{12{out_1[19]}}, out_1[19:0]};  // Bit_Extender bit_extender_1
  assign out_16 = DrOff ? out_9 : 32'bz;  // Controlled_Buffer controlled_buffer_5
  ControlUnit controlunit_1 (
    .Datain(out_1), .DrReg(DrReg), .DrMem(DrMem), .DrALU(DrALU), .DrPC(DrPC), .DrOff(DrOff), .LdPC(LdPC),
    .LdIR(LdIR), .LdMAR(LdMar), .LdA(LdA), .LdB(LdB), .LdCC(LdCC), .WrtReg(WrtReg), .WrtMem(WrMem),
    .regno(out_14), .regsel(out_12), .func(out_11), .C(CheckCC), .clc(clock));

  assign out_2 = out_1[31:28];
  assign out_19 = out_1[22:20];

  // Other names for the same wires on the sheet: a0[31:0] = out_4; a1[31:0] = out_5; a2[31:0] = out_6;
  //   at[31:0] = out_17; func[1:0] = out_11; k0[31:0] = out_22; regno[3:0] = out_14; RegSel[1:0] = out_12;
  //   s0[31:0] = out_18; s1[31:0] = out_23; s2[31:0] = out_24; t0[31:0] = out_8; t1[31:0] = out_10; t2[31:0] = out_13;
  //   v0[31:0] = out_3

  // Notes on the sheet:
  //   Yufeng Wang 
endmodule

module ALU (
  input  [31:0] A,
  input  [1:0] control,
  input  [31:0] B,
  output [31:0] Output
);

  wire [1:0] comparator_1_eq;
  wire [31:0] adder_1_out, adder_2_out, multiplexer_2_out, nand_1_out, shifter_1_out, shifter_2_out,
       shifter_3_out;

  Comparator #(.width(1), .mode("unsigned")) comparator_1 (
    .a(B[18]), .b(1'b1), .eq(comparator_1_eq[0]));  // open: gt, lt
  Comparator #(.width(1), .mode("unsigned")) comparator_2 (
    .a(B[19]), .b(1'b1), .eq(comparator_1_eq[1]));  // open: gt, lt
  Adder #(.width(32)) adder_1 (.a(A), .b(B), .out(adder_1_out));  // open: cin, cout
  assign nand_1_out = ~(A & B);  // NAND_Gate nand_1, 32 bits wide
  Adder #(.width(32)) adder_2 (.a(A), .b(32'h1), .out(adder_2_out), .cin(1'b0));  // open: cout
  Shifter #(.width(32)) shifter_1 (.in(A), .\dist (B[4:0]), .out(shifter_1_out));
  Shifter #(.width(32), .shift("lr")) shifter_2 (.in(A), .\dist (B[4:0]), .out(shifter_2_out));
  Shifter #(.width(32), .shift("ar")) shifter_3 (.in(A), .\dist (B[4:0]), .out(shifter_3_out));
  Multiplexer #(.select(2), .width(32), .disabled(0), .enable("false")) multiplexer_1 (
    .in0(adder_1_out), .in1(nand_1_out), .in2(adder_2_out), .in3(multiplexer_2_out), .out(Output),
    .sel(control));
  Multiplexer #(.select(2), .width(32), .disabled(0), .enable("false")) multiplexer_2 (
    .in0(shifter_1_out), .in1(shifter_2_out), .in2(shifter_1_out), .in3(shifter_3_out),
    .out(multiplexer_2_out), .sel(comparator_1_eq));

  // Notes on the sheet:
  //   00: add
  //   01:NAND
  //   10:A+1
  //   11:shift
endmodule

module RegisterFile (
  input  [31:0] Din,
  input  clk,
  input  [3:0] Regno,
  input  WrtReg,
  output [31:0] at,
  output [31:0] v0,
  output [31:0] a0,
  output [31:0] a1,
  output [31:0] a2,
  output [31:0] \output ,
  output [31:0] t0,
  output [31:0] t1,
  output [31:0] t2,
  output [31:0] s0,
  output [31:0] s1,
  output [31:0] s2,
  output [31:0] k0,
  output [31:0] s_prime_p,
  output [31:0] fp
);

  wire not_1_out, registerselector_1__0, registerselector_1__1, registerselector_1__2, registerselector_1__3,
       registerselector_1__4, registerselector_1__5, registerselector_1__6, registerselector_1__7,
       registerselector_1__8, registerselector_1__9, registerselector_1__10, registerselector_1__11,
       registerselector_1__12, registerselector_1__13, registerselector_1__14, registerselector_1__15;
  wire [31:0] _0, _15;

  Register #(.width(32)) register_1 (.D({32{1'b0}}), .en(registerselector_1__0), .Q(_0), .clk(clk));  // open: clr
  Register #(.width(32)) register_2 (.D(Din), .en(registerselector_1__1), .Q(at), .clk(clk));  // open: clr
  Register #(.width(32)) register_3 (.D(Din), .en(registerselector_1__8), .Q(t2), .clk(clk));  // open: clr
  Register #(.width(32)) register_4 (.D(Din), .en(registerselector_1__2), .Q(v0), .clk(clk));  // open: clr
  Register #(.width(32)) register_5 (.D(Din), .en(registerselector_1__9), .Q(s0), .clk(clk));  // open: clr
  Register #(.width(32)) register_6 (.D(Din), .en(registerselector_1__3), .Q(a0), .clk(clk));  // open: clr
  Multiplexer #(.select(4), .width(32), .disabled(0)) multiplexer_1 (
    .in0(_0), .in1(at), .in2(v0), .in3(a0), .in4(a1), .in5(a2), .in6(t0), .in7(t1), .in8(t2), .in9(s0),
    .in10(s1), .in11(s2), .in12(k0), .in13(s_prime_p), .in14(fp), .in15(_15), .out(\output ), .sel(Regno),
    .en(not_1_out));
  Register #(.width(32)) register_7 (.D(Din), .en(registerselector_1__10), .Q(s1), .clk(clk));  // open: clr
  RegisterSelector registerselector_1 (
    .RegNum(Regno), ._0(registerselector_1__0), ._1(registerselector_1__1), ._2(registerselector_1__2),
    ._3(registerselector_1__3), ._4(registerselector_1__4), ._5(registerselector_1__5),
    ._6(registerselector_1__6), ._7(registerselector_1__7), ._8(registerselector_1__8),
    ._9(registerselector_1__9), ._10(registerselector_1__10), ._11(registerselector_1__11),
    ._12(registerselector_1__12), ._13(registerselector_1__13), ._14(registerselector_1__14),
    ._15(registerselector_1__15), .WrReg(WrtReg));
  Register #(.width(32)) register_8 (.D(Din), .en(registerselector_1__4), .Q(a1), .clk(clk));  // open: clr
  Register #(.width(32)) register_9 (.D(Din), .en(registerselector_1__11), .Q(s2), .clk(clk));  // open: clr
  not not_1 (not_1_out, WrtReg);
  Register #(.width(32)) register_10 (.D(Din), .en(registerselector_1__5), .Q(a2), .clk(clk));  // open: clr
  Register #(.width(32)) register_11 (.D(Din), .en(registerselector_1__12), .Q(k0), .clk(clk));  // open: clr
  Register #(.width(32)) register_12 (.D(Din), .en(registerselector_1__6), .Q(t0), .clk(clk));  // open: clr
  Register #(.width(32)) register_13 (.D(Din), .en(registerselector_1__13), .Q(s_prime_p), .clk(clk));  // open: clr
  Register #(.width(32)) register_14 (.D(Din), .en(registerselector_1__7), .Q(t1), .clk(clk));  // open: clr
  Register #(.width(32)) register_15 (.D(Din), .en(registerselector_1__14), .Q(fp), .clk(clk));  // open: clr
  Register #(.width(32)) register_16 (.D(Din), .en(registerselector_1__15), .Q(_15), .clk(clk));  // open: clr

  // Other names for the same wires on the sheet: _1[31:0] = at; _2[31:0] = v0; _3[31:0] = a0; _4[31:0] = a1;
  //   _5[31:0] = a2; _6[31:0] = t0; _7[31:0] = t1; _8[31:0] = t2; _9[31:0] = s0; _10[31:0] = s1; _11[31:0] = s2;
  //   _12[31:0] = k0; _13[31:0] = s_prime_p; _14[31:0] = fp; clc = clk; Datain[31:0] = Din
endmodule

module RegisterSelector (
  input  [3:0] RegNum,
  input  WrReg,
  output _0,
  output _1,
  output _2,
  output _3,
  output _4,
  output _5,
  output _6,
  output _7,
  output _8,
  output _9,
  output _10,
  output _11,
  output _12,
  output _13,
  output _14,
  output _15
);

  wire decoder_1_out0, decoder_1_out1, decoder_1_out2, decoder_1_out3, decoder_1_out4, decoder_1_out5,
       decoder_1_out6, decoder_1_out7, decoder_1_out8, decoder_1_out9, decoder_1_out10, decoder_1_out11,
       decoder_1_out12, decoder_1_out13, decoder_1_out14, decoder_1_out15;

  and and_1 (_0, decoder_1_out0, WrReg);
  and and_2 (_1, decoder_1_out1, WrReg);
  and and_3 (_3, decoder_1_out3, WrReg);
  and and_4 (_2, decoder_1_out2, WrReg);
  and and_5 (_4, decoder_1_out4, WrReg);
  and and_6 (_5, decoder_1_out5, WrReg);
  Decoder #(.select(4)) decoder_1 (
    .out0(decoder_1_out0), .out1(decoder_1_out1), .out2(decoder_1_out2), .out3(decoder_1_out3),
    .out4(decoder_1_out4), .out5(decoder_1_out5), .out6(decoder_1_out6), .out7(decoder_1_out7),
    .out8(decoder_1_out8), .out9(decoder_1_out9), .out10(decoder_1_out10), .out11(decoder_1_out11),
    .out12(decoder_1_out12), .out13(decoder_1_out13), .out14(decoder_1_out14), .out15(decoder_1_out15),
    .sel(RegNum), .en(1'b1));
  and and_7 (_6, decoder_1_out6, WrReg);
  and and_8 (_7, decoder_1_out7, WrReg);
  and and_9 (_8, decoder_1_out8, WrReg);
  and and_10 (_9, decoder_1_out9, WrReg);
  and and_11 (_10, decoder_1_out10, WrReg);
  and and_12 (_11, decoder_1_out11, WrReg);
  and and_13 (_12, decoder_1_out12, WrReg);
  and and_14 (_13, decoder_1_out13, WrReg);
  and and_15 (_14, decoder_1_out14, WrReg);
  and and_16 (_15, decoder_1_out15, WrReg);
endmodule

module ControlUnit (
  input  [31:0] Datain,
  input  C,
  input  clc,
  output DrReg,
  output DrMem,
  output DrALU,
  output DrPC,
  output DrOff,
  output LdPC,
  output LdIR,
  output LdMAR,
  output LdA,
  output LdB,
  output LdCC,
  output WrtReg,
  output WrtMem,
  output [3:0] regno,
  output [1:0] regsel,
  output [1:0] func
);

  wire Optest;
  wire [5:0] multiplexer_2_out, register_1_q, rom_2_data, rom_3_data;
  wire [24:0] rom_1_data;

  ROM #(.addrWidth(6), .dataWidth(25)) rom_1 (
    .addr(register_1_q),
    .data({rom_1_data[24], Optest, func, regsel, WrtMem, WrtReg, LdCC, LdB, LdA, LdMAR, LdIR, LdPC, DrOff, DrPC, DrALU, DrMem, DrReg, rom_1_data[5:0]}));  // open: sel
  ROM #(.addrWidth(4), .dataWidth(6)) rom_2 (.addr(Datain[31:28]), .data(rom_2_data));  // open: sel
  ROM #(.addrWidth(2), .dataWidth(6)) rom_3 (.addr({1'b0, C}), .data(rom_3_data));  // open: sel
  Multiplexer #(.select(2), .width(4), .disabled(0)) multiplexer_1 (
    .in0(Datain[27:24]), .in1(Datain[23:20]), .in2(Datain[3:0]), .out(regno), .sel(regsel), .en(1'b1));  // open: in3
  Multiplexer #(.select(2), .width(6), .disabled(0)) multiplexer_2 (
    .in0(rom_1_data[5:0]), .in1(rom_3_data), .in2(rom_2_data), .out(multiplexer_2_out),
    .sel({Optest, rom_1_data[24]}), .en(1'b1));  // open: in3
  Register #(.width(6)) register_1 (.D(multiplexer_2_out), .Q(register_1_q), .clk(clc));  // open: en, clr

  // Notes on the sheet:
  //   contents of rom_1 (hex, n*v repeats v):
  //   6201 1082 c00900 84044 108045 30100 84047 8408 30100 8404a 10804b 230100 2020d 80840 8404f 8410 2111
  //   30080 4213 8414 30100 84056 8417 2118 40040 8405a 841b 63011c 10000 1000000 421f 8420 900 22 21 22
  //   contents of rom_2 (hex, n*v repeats v):
  //   3 6 9 1d c e 12 15 19 6*0 21
  //   contents of rom_3 (hex, n*v repeats v):
  //   0 1e
endmodule

module QieKCC (
  input  [2:0] in_1,
  input  [2:0] in_2,
  output \output 
);

  wire and_1_out, and_2_out, and_3_out;

  and and_1 (and_1_out, in_2[0], in_1[0]);
  and and_2 (and_2_out, in_1[1], in_2[1]);
  and and_3 (and_3_out, in_1[2], in_2[2]);
  or or_1 (\output , and_1_out, and_2_out, and_3_out);
endmodule
