// Logisim project Wang_Yufeng.circ as structural Verilog: 10 circuits, main circuit main
module main (
  output [3:0] out_1,
  output [31:0] out_2,
  output [31:0] out_3,
  output [3:0] out_4,
  output [31:0] out_5,
  output [31:0] out_6,
  output [31:0] out_7,
  output [31:0] out_8,
  output [3:0] out_9,
  output [3:0] out_10,
  output [1:0] out_11,
  output [3:0] out_12,
  output [3:0] out_13,
  output [3:0] out_14,
  output [31:0] out_15,
  output [31:0] out_16,
  output [31:0] out_17,
  output [3:0] out_18,
  output [3:0] out_19,
  output [31:0] out_20,
  output [3:0] out_21,
  output [31:0] out_22,
  output [31:0] out_23,
  output [3:0] out_24,
  output [3:0] out_25,
  output [31:0] out_26,
  output [3:0] out_27,
  output [31:0] out_28,
  output [3:0] out_29,
  output [3:0] out_30,
  output [3:0] out_31,
  output [31:0] out_32,
  output [31:0] out_33,
  output [31:0] out_34,
  output [31:0] out_35,
  output [31:0] out_36,
  output [31:0] out_37,
  output [31:0] out_38,
  output [31:0] out_39,
  output [31:0] out_40,
  output [31:0] out_41,
  output [31:0] out_42,
  output [31:0] out_43,
  output [31:0] out_44
);

  wire and_1_out, and_2_out, and_4_out, and_5_out, BRANCH, button_1_out, clc, comparator_1_eq,
       comparator_2_eq, comparator_3_eq, comparator_4_eq, comparator_5_eq, comparator_6_eq, comparator_7_eq,
       comparator_9_eq, comparator_10_eq, comparator_11_eq, comparator_12_eq, comparator_13_eq,
       comparator_14_eq, comparator_15_gt, Disable, EN, ex_mem_buffer_1_ld, ex_mem_buffer_1_wr, Flush, NoOp,
       not_1_out, or_2_out, or_3_out, or_4_out, STALL, takebranch, WB;
  wire [1:0] PCSel;
  wire [3:0] REGSEL2, Rz, WBReg, WBRx, WBRy;
  wire [31:0] adder_2_out, adder_3_out, counter_1_q, EXNewPC, EXoffSet, Expass, FOUT1, FOUT2,
       idrr_ex_buffer_1_selected, MEMoffSet, MEMRdata1, MEMRdata2, multiplexer_1_out, multiplexer_2_out,
       multiplexer_3_out, NewPC, offset, ram_1_data, register_1_q, WBdata;

  not not_1 (not_1_out, Disable);
  Register #(.width(32)) register_1 (.D(multiplexer_1_out), .en(and_1_out), .Q(register_1_q), .clk(clc));  // open: clr
  and and_1 (and_1_out, EN, not_1_out);
  Multiplexer #(.select(2), .width(32)) multiplexer_1 (
    .in0(NewPC), .in1(out_17), .in2(MEMRdata1), .in3(register_1_q), .out(multiplexer_1_out), .sel(PCSel));  // open: en
  Comparator #(.width(4)) comparator_1 (.a(out_19), .b(4'b0000), .eq(comparator_1_eq));  // open: gt, lt
  Comparator #(.width(4)) comparator_2 (.a(out_19), .b(4'b0010), .eq(comparator_2_eq));  // open: gt, lt
  or or_1 (Flush, PCSel[0], PCSel[1]);
  Clock CLOCK (.out(clc));
  Comparator #(.width(4)) comparator_3 (.a(out_21), .b(4'b0101), .eq(comparator_3_eq));  // open: gt, lt
  Comparator #(.width(4)) comparator_4 (.a(out_21), .b(4'b0110), .eq(comparator_4_eq));  // open: gt, lt
  Comparator #(.width(4)) comparator_5 (.a(out_14), .b(out_4), .eq(comparator_5_eq));  // open: gt, lt
  Comparator #(.width(4)) comparator_6 (.a(out_14), .b(Rz), .eq(comparator_6_eq));  // open: gt, lt
  Adder #(.width(32)) adder_1 (.a(register_1_q), .b(32'h1), .out(NewPC));  // open: cin, cout
  or or_2 (or_2_out, comparator_1_eq, comparator_2_eq);
  Register #(.width(1)) register_2 (.D(STALL), .Q(NoOp), .clk(clc));  // open: en, clr
  or or_3 (or_3_out, comparator_3_eq, comparator_4_eq);
  and and_2 (and_2_out, comparator_6_eq, or_2_out);
  RAM #(.addrWidth(24), .dataWidth(32)) ram_1 (
    .addr(register_1_q[23:0]), .data(ram_1_data), .sel(and_1_out));  // open: clk, ld, clr
  or or_4 (or_4_out, comparator_5_eq, and_2_out);
  Multiplexer #(.width(32)) multiplexer_2 (
    .in0(ram_1_data), .in1({32{1'b0}}), .out(multiplexer_2_out), .sel(Disable));  // open: en
  IF_IDRR_Buffer IF_IDRR (
    .Data(multiplexer_2_out), .PC(NewPC), .Opcode(out_19), .Rx(out_1), .Ry(out_4), .offset(offset), .Rz(Rz),
    .PCout(out_6), .Clear(Flush), .EN(EN), .Clock(clc), .REGno2(out_9));
  and and_3 (STALL, or_3_out, or_4_out);
  Counter #(.width(32), .max('hffffffff)) counter_1 (
    .count(comparator_7_eq), .Q(counter_1_q), .clk(clc), .clr(button_1_out));  // open: load, D, carry
  Comparator #(.width(4)) comparator_7 (.a(out_19), .b(4'b1111), .eq(comparator_7_eq));  // open: gt, lt
  Button button_1 (.out(button_1_out));
  Comparator #(.width(32)) comparator_8 (.a(counter_1_q), .b({32{1'b0}}), .gt(Disable));  // open: eq, lt
  Multiplexer #(.width(32)) multiplexer_3 (
    .in0(out_28), .in1(out_17), .out(multiplexer_3_out), .sel(comparator_9_eq));  // open: en
  Comparator #(.width(4)) comparator_9 (.a(out_25), .b(4'b0110), .eq(comparator_9_eq));  // open: gt, lt
  Forwarding forwarding_1 (
    .Result_EX(Expass), .DATA_MEM(out_16), .OUT1(out_2), .EXRX(out_14), .OPCODE_IF(out_19), .MEMRX(out_12),
    .OPCODE_EX(out_21), .WBRX(WBRx), .Result_MEM(multiplexer_3_out), .OPCODE_WB(out_29), .OUT2(out_3),
    .Ry_IDRR(out_4), .Result_WB(WBdata), .RSel_IDRR(REGSEL2), .FOUT2(FOUT1), .FOUT1(FOUT2),
    .OPCODE_MEM(out_25));
  Dual_Ported_Register_File dual_ported_register_file_1 (
    .CLK(clc), .WrEN(WB), .OUT1(out_2), .WrREGNO(WBReg), .RdREGNO1(out_4), .RdREGNO2(out_9), .OUT2(out_3),
    .INPUT(WBdata), .a0(out_32), .a1(out_36), .a2(out_39), .t1(out_37), .t2(out_40), .to(out_33),
    .s0(out_34), .s1(out_38), .s2(out_41), .at(out_44), .ra(out_43), .v0(out_42), .k0(out_35));
  Multiplexer #(.enable("false")) multiplexer_4 (.in0(1'b1), .in1(1'b0), .out(EN), .sel(STALL));
  Comparator #(.width(4)) comparator_10 (.a(out_21), .b(4'b0011), .eq(comparator_10_eq));  // open: gt, lt
  Comparator #(.width(32)) comparator_11 (.a(out_15), .b(out_26), .eq(comparator_11_eq));  // open: gt, lt
  Comparator #(.width(4)) comparator_12 (.a(out_21), .b(4'b1001), .eq(comparator_12_eq));  // open: gt, lt
  Adder #(.width(32)) adder_2 (.a(EXNewPC), .b(EXoffSet), .out(adder_2_out));  // open: cin, cout
  IDRR_EX_Buffer idrr_ex_buffer_1 (
    .PC(out_6), .Opcode(out_19), .Rx(out_1), .imm(offset), .put1(FOUT1), .put2(FOUT2), .clc(clc),
    .newpc(EXNewPC), .newopc(out_21), .newrx(out_14), .newimm(EXoffSet), .newput1(out_15), .newput2(out_26),
    .Ry(out_4), .Flush(Flush), .En(EN), .newry(out_18), .Noop(NoOp), .func(out_11),
    .selected(idrr_ex_buffer_1_selected));
  Comparator #(.width(32)) comparator_13 (.a(out_15), .b(out_26), .eq(comparator_13_eq));  // open: gt, lt
  and and_4 (and_4_out, comparator_10_eq, comparator_11_eq);
  and and_5 (and_5_out, ~comparator_13_eq, comparator_12_eq);  // AND_Gate
  Multiplexer #(.width(32)) multiplexer_5 (
    .in0(out_20), .in1(adder_2_out), .out(Expass), .sel(comparator_14_eq));  // open: en
  Comparator #(.width(4)) comparator_14 (.a(out_25), .b(4'b0110), .eq(comparator_14_eq));  // open: gt, lt
  Comparator #(.width(4), .mode("unsigned")) comparator_15 (
    .a(out_19), .b(4'b0010), .gt(comparator_15_gt));  // open: eq, lt
  or or_5 (BRANCH, and_4_out, and_5_out);
  ALU alu_1 (.A(out_15), .B(idrr_ex_buffer_1_selected), .Output(out_20), .control(out_11));
  Multiplexer #(.width(4)) multiplexer_6 (.in0(Rz), .in1(out_1), .out(REGSEL2), .sel(comparator_15_gt));  // open: en
  Adder #(.width(32)) adder_3 (.a(EXNewPC), .b(EXoffSet), .out(adder_3_out));  // open: cin, cout
  EX_MEM_Buffer ex_mem_buffer_1 (
    .EN(1'b1), .Clock(clc), .Rdata1IN(out_15), .Rdata2_IN(out_26), .Result_IN(out_20), .OPCODE_EX(out_21),
    .Rx_In(out_14), .Ry_In(out_18), .PC_1_IN(EXNewPC), .BRANCH(BRANCH), .Pc_1_offset(adder_3_out),
    .Rdata1_OUT(MEMRdata1), .Rdata2_OUT(MEMRdata2), .Result_Out(out_28), .OPCODE_EX_2(out_25),
    .Rx_OUT(out_12), .Ry_OUT(out_10), .PC_1_OUT(out_7), .BRANCH_2(takebranch), .Pc_1_offset_2(out_17),
    .Offset_OUT(MEMoffSet), .Offset_IN(EXoffSet), .LD(ex_mem_buffer_1_ld), .WR(ex_mem_buffer_1_wr));
  MEMcontrol memcontrol_1 (
    .clk(clc), .result_mem(out_28), .opcode_mem(out_25), .rdata2__mem(MEMRdata2), .take_branch(takebranch),
    .RAM_mem(out_16), .PCsel(PCSel), .S(ex_mem_buffer_1_wr), .L(ex_mem_buffer_1_ld));
  MEM_WB_Buffer mem_wb_buffer_1 (
    .PC_1_IN(out_7), .Result_IN(out_28), .RAM_in(out_16), .OPCODE_IN(out_25), .Rx_In(out_12), .Ry_In(out_10),
    .EN(1'b1), .Clock(clc), .PC_1_OUT(out_5), .Result_Out(out_8), .OPCODE_OUT(out_29), .Rx_OUT(WBRx),
    .Ry_OUT(WBRy), .RegDatain(WBdata), .WB(WB), .RegtoWB(WBReg), .PC_kff(out_17));  // open: RAM_OUT

  assign out_13 = out_12;
  assign out_22 = out_17;
  assign out_23 = out_15;
  assign out_24 = out_14;
  assign out_27 = out_18;
  assign out_30 = out_25;
  assign out_31 = out_21;

  // Other names for the same wires on the sheet: a0[31:0] = out_32; a1[31:0] = out_36; a3[31:0] = out_39;
  //   at[31:0] = out_44; EXopcode[3:0] = out_21; EXRdata1[31:0] = out_15; EXRdata2[31:0] = out_26; EXRx[3:0] = out_14;
  //   EXRy[3:0] = out_18; k0[31:0] = out_35; MEMNewPC[31:0] = out_7; MEMopcode[3:0] = out_25;
  //   MEMPC_OFFset[31:0] = out_17; MEMResult[31:0] = out_28; MEMRx[3:0] = out_12; MEMRy[3:0] = out_10;
  //   NewPC_if[31:0] = out_6; Opcode[3:0] = out_19; ra[31:0] = out_43; RAM_MEM[31:0] = out_16; RegNo2[3:0] = out_9;
  //   result[31:0] = out_20; Rx[3:0] = out_1; Ry[3:0] = out_4; s0[31:0] = out_34; s1[31:0] = out_38;
  //   s2[31:0] = out_41; Src1[31:0] = out_2; Src2[31:0] = out_3; t0[31:0] = out_33; t1[31:0] = out_37;
  //   t2[31:0] = out_40; v0[31:0] = out_42; WBnewPC[31:0] = out_5; WBOpcode[3:0] = out_29; WBresult[31:0] = out_8

  // Notes on the sheet:
  //   WANG YUFENG
endmodule

module Dual_Ported_Register_File (
  input  CLK,
  input  WrEN,
  input  [3:0] WrREGNO,
  input  [3:0] RdREGNO1,
  input  [3:0] RdREGNO2,
  input  [31:0] INPUT,
  output [31:0] OUT1,
  output [31:0] a0,
  output [31:0] a1,
  output [31:0] OUT2,
  output [31:0] a2,
  output [31:0] to,
  output [31:0] t1,
  output [31:0] t2,
  output [31:0] s0,
  output [31:0] s1,
  output [31:0] s2,
  output [31:0] at,
  output [31:0] ra,
  output [31:0] v0,
  output [31:0] k0
);

  wire En_a0, En_a1, En_a2, En_at, En_fp, En_k0, En_ra, En_s0, En_s1, En_s2, En_sp, En_t0, En_t1, En_t2,
       En_v0;
  wire [31:0] fp, sp, zero;

  Decoder #(.select(4), .disabled(0)) decoder_1 (
    .out1(En_at), .out2(En_v0), .out3(En_a0), .out4(En_a1), .out5(En_a2), .out6(En_t0), .out7(En_t1),
    .out8(En_t2), .out9(En_s0), .out10(En_s1), .out11(En_s2), .out12(En_k0), .out13(En_sp), .out14(En_fp),
    .out15(En_ra), .sel(WrREGNO), .en(WrEN));  // open: out0
  Register #(.width(32)) u_zero (.D(INPUT), .en(1'b0), .Q(zero), .clk(CLK));  // open: clr
  Register #(.width(32)) u_at (.D(INPUT), .en(En_at), .Q(at), .clk(CLK));  // open: clr
  Register #(.width(32)) u_v0 (.D(INPUT), .en(En_v0), .Q(v0), .clk(CLK));  // open: clr
  Register #(.width(32)) u_a0 (.D(INPUT), .en(En_a0), .Q(a0), .clk(CLK));  // open: clr
  Register #(.width(32)) u_a1 (.D(INPUT), .en(En_a1), .Q(a1), .clk(CLK));  // open: clr
  Register #(.width(32)) u_a2 (.D(INPUT), .en(En_a2), .Q(a2), .clk(CLK));  // open: clr
  Register #(.width(32)) t0 (.D(INPUT), .en(En_t0), .Q(to), .clk(CLK));  // open: clr
  Register #(.width(32)) u_t1 (.D(INPUT), .en(En_t1), .Q(t1), .clk(CLK));  // open: clr
  Multiplexer #(.select(4), .width(32), .disabled(0), .enable("false")) multiplexer_1 (
    .in0(zero), .in1(at), .in2(v0), .in3(a0), .in4(a1), .in5(a2), .in6(to), .in7(t1), .in8(t2), .in9(s0),
    .in10(s1), .in11(s2), .in12(k0), .in13(sp), .in14(fp), .in15(ra), .out(OUT2), .sel(RdREGNO2));
  Register #(.width(32)) u_t2 (.D(INPUT), .en(En_t2), .Q(t2), .clk(CLK));  // open: clr
  Register #(.width(32)) u_s0 (.D(INPUT), .en(En_s0), .Q(s0), .clk(CLK));  // open: clr
  Register #(.width(32)) u_s1 (.D(INPUT), .en(En_s1), .Q(s1), .clk(CLK));  // open: clr
  Register #(.width(32)) u_s2 (.D(INPUT), .en(En_s2), .Q(s2), .clk(CLK));  // open: clr
  Register #(.width(32)) u_k0 (.D(INPUT), .en(En_k0), .Q(k0), .clk(CLK));  // open: clr
  Register #(.width(32)) u_sp (.D(INPUT), .en(En_sp), .Q(sp), .clk(CLK));  // open: clr
  Register #(.width(32)) u_fp (.D(INPUT), .en(En_fp), .Q(fp), .clk(CLK));  // open: clr
  Register #(.width(32)) u_ra (.D(INPUT), .en(En_ra), .Q(ra), .clk(CLK));  // open: clr
  Multiplexer #(.select(4), .width(32), .disabled(0), .enable("false")) multiplexer_2 (
    .in0(zero), .in1(at), .in2(v0), .in3(a0), .in4(a1), .in5(a2), .in6(to), .in7(t1), .in8(t2), .in9(s0),
    .in10(s1), .in11(s2), .in12(k0), .in13(sp), .in14(fp), .in15(ra), .out(OUT1), .sel(RdREGNO1));

  // Other names for the same wires on the sheet: t0[31:0] = to

  // Notes on the sheet:
  //   MODIFY AT YOUR OWN RISK
endmodule

// IF/IDRR
module IF_IDRR_Buffer (
  input  [31:0] Data,
  input  [31:0] PC,
  input  Clear,
  input  EN,
  input  Clock,
  output [3:0] Opcode,
  output [3:0] Rx,
  output [3:0] Ry,
  output [31:0] offset,
  output [3:0] Rz,
  output [3:0] REGno2,
  output [31:0] PCout
);

  wire comparator_1_eq, comparator_2_eq, or_1_out;
  wire [19:4] register_1_q;

  Register #(.width(32)) register_1 (
    .D(Data), .en(EN), .Q({Opcode, Rx, Ry, register_1_q, Rz}), .clk(Clock), .clr(Clear));
  Register #(.width(32)) register_2 (.D(PC), .en(EN), .Q(PCout), .clk(Clock), .clr(Clear));
  assign offset = {{12{register_1_q[19]}}, {register_1_q, Rz}};  // Bit_Extender bit_extender_1
  Comparator #(.width(4)) comparator_1 (.a(Opcode), .b(4'b0000), .eq(comparator_1_eq));  // open: gt, lt
  Comparator #(.width(4)) comparator_2 (.a(Opcode), .b(4'b0010), .eq(comparator_2_eq));  // open: gt, lt
  or or_1 (or_1_out, comparator_1_eq, comparator_2_eq);
  Multiplexer #(.width(4), .enable("false")) multiplexer_1 (.in0(Rx), .in1(Rz), .out(REGno2), .sel(or_1_out));

  // Other names for the same wires on the sheet: clc = Clock; CLR = Clear
endmodule

module IDRR_EX_Buffer (
  input  [31:0] PC,
  input  [3:0] Opcode,
  input  [3:0] Rx,
  input  [3:0] Ry,
  input  [31:0] imm,
  input  [31:0] put1,
  input  [31:0] put2,
  input  Flush,
  input  En,
  input  clc,
  input  Noop,
  output [31:0] newpc,
  output [3:0] newopc,
  output [3:0] newrx,
  output [3:0] newry,
  output [31:0] newimm,
  output [31:0] newput1,
  output [31:0] newput2,
  output [31:0] selected,
  output [1:0] func
);

  wire comparator_1_eq, comparator_2_eq, comparator_3_eq, comparator_4_eq, or_1_out;
  wire [3:0] register_2_q, register_3_q, register_4_q;
  wire [31:0] register_1_q, register_5_q, register_6_q, register_7_q;

  Register #(.width(32)) register_1 (.D(PC), .en(En), .Q(register_1_q), .clk(clc), .clr(Flush));
  Register #(.width(4)) register_2 (.D(Opcode), .en(En), .Q(register_2_q), .clk(clc), .clr(Flush));
  Register #(.width(4)) register_3 (.D(Rx), .en(En), .Q(register_3_q), .clk(clc), .clr(Flush));
  Register #(.width(4)) register_4 (.D(Ry), .en(En), .Q(register_4_q), .clk(clc), .clr(Flush));
  Register #(.width(32)) register_5 (.D(imm), .en(En), .Q(register_5_q), .clk(clc), .clr(Flush));
  Register #(.width(32)) register_6 (.D(put1), .en(En), .Q(register_6_q), .clk(clc), .clr(Flush));
  Register #(.width(32)) register_7 (.D(put2), .en(En), .Q(register_7_q), .clk(clc), .clr(Flush));
  Multiplexer #(.width(32)) multiplexer_1 (.in0(register_1_q), .in1({32{1'b0}}), .out(newpc), .sel(Noop));  // open: en
  Multiplexer #(.width(4)) multiplexer_2 (.in0(register_2_q), .in1(4'b0000), .out(newopc), .sel(Noop));  // open: en
  Multiplexer #(.width(4)) multiplexer_3 (.in0(register_3_q), .in1(4'b0000), .out(newrx), .sel(Noop));  // open: en
  Multiplexer #(.width(4)) multiplexer_4 (.in0(register_4_q), .in1(4'b0000), .out(newry), .sel(Noop));  // open: en
  Multiplexer #(.width(32)) multiplexer_5 (.in0(register_5_q), .in1({32{1'b0}}), .out(newimm), .sel(Noop));  // open: en
  Multiplexer #(.width(32)) multiplexer_6 (
    .in0(register_6_q), .in1({32{1'b0}}), .out(newput1), .sel(Noop));  // open: en
  Multiplexer #(.width(32)) multiplexer_7 (
    .in0(register_7_q), .in1({32{1'b0}}), .out(newput2), .sel(Noop));  // open: en
  Comparator #(.width(4)) comparator_1 (.a(newopc), .b(4'b0000), .eq(comparator_1_eq));  // open: gt, lt
  Comparator #(.width(4)) comparator_2 (.a(newopc), .b(4'b0010), .eq(comparator_2_eq));  // open: gt, lt
  Comparator #(.width(4)) comparator_3 (.a(newopc), .b(4'b0010), .eq(comparator_3_eq));  // open: gt, lt
  Comparator #(.width(4)) comparator_4 (.a(newopc), .b(4'b1000), .eq(comparator_4_eq));  // open: gt, lt
  Multiplexer #(.width(32), .enable("false")) multiplexer_8 (
    .in0(newimm), .in1(newput2), .out(selected), .sel(or_1_out));
  or or_1 (or_1_out, comparator_1_eq, comparator_2_eq);
  or or_2 (func[0], comparator_3_eq, comparator_4_eq);
  Comparator #(.width(4)) comparator_5 (.a(newopc), .b(4'b1000), .eq(func[1]));  // open: gt, lt
endmodule

module EX_MEM_Buffer (
  input  EN,
  input  Clock,
  input  [31:0] Offset_IN,
  input  [31:0] Rdata1IN,
  input  [31:0] Rdata2_IN,
  input  [31:0] Result_IN,
  input  [3:0] OPCODE_EX,
  input  [3:0] Rx_In,
  input  [3:0] Ry_In,
  input  [31:0] PC_1_IN,
  input  BRANCH,
  input  [31:0] Pc_1_offset,
  output [31:0] Offset_OUT,
  output [31:0] Rdata1_OUT,
  output [31:0] Rdata2_OUT,
  output [31:0] Result_Out,
  output [3:0] OPCODE_EX_2,
  output [3:0] Rx_OUT,
  output [3:0] Ry_OUT,
  output [31:0] PC_1_OUT,
  output BRANCH_2,
  output [31:0] Pc_1_offset_2,
  output LD,
  output WR
);

  wire comparator_1_eq, comparator_2_eq;

  Comparator #(.width(4)) comparator_1 (.a(OPCODE_EX), .b(4'b0101), .eq(comparator_1_eq));  // open: gt, lt
  Comparator #(.width(4)) comparator_2 (.a(OPCODE_EX), .b(4'b0111), .eq(comparator_2_eq));  // open: gt, lt
  Register #(.width(32)) Rdata1 (.D(Offset_IN), .Q(Offset_OUT), .clk(Clock));  // open: en, clr
  Register #(.width(32)) Rdata1_2 (.D(Rdata1IN), .en(EN), .Q(Rdata1_OUT), .clk(Clock));  // open: clr
  Register #(.width(32)) Rdata2 (.D(Rdata2_IN), .en(EN), .Q(Rdata2_OUT), .clk(Clock));  // open: clr
  Register #(.width(32)) RESULT (.D(Result_IN), .en(EN), .Q(Result_Out), .clk(Clock));  // open: clr
  Register #(.width(4)) OPCODE (.D(OPCODE_EX), .en(EN), .Q(OPCODE_EX_2), .clk(Clock));  // open: clr
  Register #(.width(4)) Rx (.D(Rx_In), .en(EN), .Q(Rx_OUT), .clk(Clock));  // open: clr
  Register #(.width(4)) Ry (.D(Ry_In), .en(EN), .Q(Ry_OUT), .clk(Clock));  // open: clr
  Register #(.width(32)) PC_1 (.D(PC_1_IN), .en(EN), .Q(PC_1_OUT), .clk(Clock));  // open: clr
  Register #(.width(1)) u_BRANCH (.D(BRANCH), .en(EN), .Q(BRANCH_2), .clk(Clock));  // open: clr
  Register #(.width(32)) NEWPC (.D(Pc_1_offset), .en(EN), .Q(Pc_1_offset_2), .clk(Clock));  // open: clr
  Register #(.width(1)) u_LD (.D(comparator_1_eq), .en(EN), .Q(LD), .clk(Clock));  // open: clr
  Register #(.width(1)) u_WR (.D(comparator_2_eq), .en(EN), .Q(WR), .clk(Clock));  // open: clr
endmodule

module MEM_WB_Buffer (
  input  [31:0] PC_1_IN,
  input  [31:0] PC_kff,
  input  [31:0] Result_IN,
  input  [31:0] RAM_in,
  input  [3:0] OPCODE_IN,
  input  [3:0] Rx_In,
  input  [3:0] Ry_In,
  input  EN,
  input  Clock,
  output [31:0] PC_1_OUT,
  output [31:0] Result_Out,
  output [31:0] RAM_OUT,
  output [3:0] OPCODE_OUT,
  output [3:0] Rx_OUT,
  output [3:0] Ry_OUT,
  output [31:0] RegDatain,
  output WB,
  output [3:0] RegtoWB
);

  wire and_1_out, comparator_1_eq, comparator_2_eq, comparator_3_eq, comparator_4_lt, comparator_5_gt,
       comparator_6_lt, comparator_7_eq, comparator_8_eq;
  wire [1:0] or_1_out;
  wire [31:0] PC_off;

  Comparator #(.width(4)) comparator_1 (.a(OPCODE_OUT), .b(4'b0101), .eq(comparator_1_eq));  // open: gt, lt
  Comparator #(.width(4)) comparator_2 (.a(OPCODE_OUT), .b(4'b0110), .eq(comparator_2_eq));  // open: gt, lt
  Comparator #(.width(4)) comparator_3 (.a(OPCODE_OUT), .b(4'b0100), .eq(comparator_3_eq));  // open: gt, lt
  Comparator #(.width(4)) comparator_4 (.a(OPCODE_OUT), .b(4'b0011), .lt(comparator_4_lt));  // open: gt, eq
  Comparator #(.width(4)) comparator_5 (.a(OPCODE_OUT), .b(4'b0011), .gt(comparator_5_gt));  // open: eq, lt
  Comparator #(.width(4)) comparator_6 (.a(OPCODE_OUT), .b(4'b0111), .lt(comparator_6_lt));  // open: gt, eq
  Comparator #(.width(4)) comparator_7 (.a(OPCODE_OUT), .b(4'b1000), .eq(comparator_7_eq));  // open: gt, lt
  Comparator #(.width(4)) comparator_8 (.a(OPCODE_OUT), .b(4'b0100), .eq(comparator_8_eq));  // open: gt, lt
  Register #(.width(32)) PC_1 (.D(PC_1_IN), .en(EN), .Q(PC_1_OUT), .clk(Clock));  // open: clr
  Register #(.width(32)) PC_iff (.D(PC_kff), .en(EN), .Q(PC_off), .clk(Clock));  // open: clr
  Register #(.width(32)) RESULT (.D(Result_IN), .en(EN), .Q(Result_Out), .clk(Clock));  // open: clr
  Register #(.width(32)) RAM (.D(RAM_in), .en(EN), .Q(RAM_OUT), .clk(Clock));  // open: clr
  Register #(.width(4)) OPCODE (.D(OPCODE_IN), .en(EN), .Q(OPCODE_OUT), .clk(Clock));  // open: clr
  Register #(.width(4)) Rx (.D(Rx_In), .en(EN), .Q(RegtoWB), .clk(Clock));  // open: clr
  Register #(.width(4)) Ry (.D(Ry_In), .en(EN), .Q(Ry_OUT), .clk(Clock));  // open: clr
  or or_1 (or_1_out[0], comparator_1_eq, comparator_2_eq);
  and and_1 (and_1_out, comparator_5_gt, comparator_6_lt);
  Multiplexer #(.select(2), .width(32), .enable("false")) multiplexer_1 (
    .in0(Result_Out), .in1(RAM_OUT), .in2(PC_1_OUT), .in3(PC_off), .out(RegDatain), .sel(or_1_out));
  or or_2 (WB, comparator_4_lt, and_1_out, comparator_7_eq);
  or or_3 (or_1_out[1], comparator_3_eq, comparator_2_eq);

  assign Rx_OUT = RegtoWB;

  // Other names for the same wires on the sheet: PC_1[31:0] = PC_1_OUT; ram[31:0] = RAM_OUT;
  //   Result[31:0] = Result_Out; Rx[3:0] = RegtoWB; Ry[3:0] = Ry_OUT
endmodule

module ALU (
  input  [31:0] A,
  input  [31:0] B,
  input  [1:0] control,
  output [31:0] Output
);

  wire [1:0] comparator_1_eq;
  wire [31:0] adder_1_out, adder_2_out, multiplexer_2_out, nand_1_out, shifter_1_out, shifter_2_out,
       shifter_3_out;

  Comparator #(.width(1), .mode("unsigned")) comparator_1 (
    .a(B[18]), .b(1'b1), .eq(comparator_1_eq[0]));  // open: gt, lt
  Comparator #(.width(1), .mode("unsigned")) comparator_2 (
    .a(B[19]), .b(1'b1), .eq(comparator_1_eq[1]));  // open: gt, lt
  Adder #(.width(32)) adder_1 (.a(A), .b(B), .out(adder_1_out));  // open: cin, cout
  assign nand_1_out = ~(A & B);  // NAND_Gate nand_1, 32 bits wide
  Adder #(.width(32)) adder_2 (.a(A), .b(32'h1), .out(adder_2_out), .cin(1'b0));  // open: cout
  Shifter #(.width(32)) shifter_1 (.in(A), .\dist (B[4:0]), .out(shifter_1_out));
  Shifter #(.width(32), .shift("lr")) shifter_2 (.in(A), .\dist (B[4:0]), .out(shifter_2_out));
  Shifter #(.width(32), .shift("ar")) shifter_3 (.in(A), .\dist (B[4:0]), .out(shifter_3_out));
  Multiplexer #(.select(2), .width(32), .disabled(0), .enable("false")) multiplexer_1 (
    .in0(adder_1_out), .in1(nand_1_out), .in2(adder_2_out), .in3(multiplexer_2_out), .out(Output),
    .sel(control));
  Multiplexer #(.select(2), .width(32), .disabled(0), .enable("false")) multiplexer_2 (
    .in0(shifter_1_out), .in1(shifter_2_out), .in2(shifter_1_out), .in3(shifter_3_out),
    .out(multiplexer_2_out), .sel(comparator_1_eq));

  // Notes on the sheet:
  //   00: add
  //   01:NAND
  //   10:A+1
  //   11:shift
endmodule

module Forwarding (
  input  [3:0] EXRX,
  input  [3:0] OPCODE_IF,
  input  [3:0] MEMRX,
  input  [3:0] WBRX,
  input  [31:0] DATA_MEM,
  input  [31:0] OUT1,
  input  [31:0] Result_EX,
  input  [31:0] Result_MEM,
  input  [31:0] OUT2,
  input  [31:0] Result_WB,
  input  [3:0] OPCODE_EX,
  input  [3:0] Ry_IDRR,
  input  [3:0] RSel_IDRR,
  input  [3:0] OPCODE_MEM,
  input  [3:0] OPCODE_WB,
  output [31:0] FOUT2,
  output [31:0] FOUT1
);

  wire comparator_1_lt, comparator_2_eq, comparator_3_eq, comparator_4_eq, comparator_5_eq, comparator_6_lt,
       comparator_7_eq, comparator_8_eq, comparator_9_eq, comparator_10_eq, comparator_11_lt,
       comparator_12_eq, comparator_13_eq, comparator_14_eq, comparator_15_eq, comparator_16_eq,
       comparator_17_eq, comparator_18_eq, comparator_19_eq, comparator_20_eq, comparator_21_eq,
       comparator_22_eq, comparator_23_eq, comparator_24_eq, comparator_25_eq, comparator_26_eq,
       comparator_27_eq, comparator_28_eq, EXRx_Ry, EXRx_Rz, MEMFRy, MEMFRz, MEMRx_Ry, MEMRx_Rz, not_1_out,
       not_2_out, not_3_out, not_4_out, not_5_out, not_6_out, not_7_out, not_8_out, not_9_out, not_10_out,
       Possible_EX_F, Possible_MEM_F, Possible_WB_F, WB_Forwad_Ry, WB_Forwad_Rz_Rx, WBFRy, WBFRz, WBRx_Ry,
       WBRx_Rz;
  wire [1:0] ResultSel_Ry, ResultSel_Rz_Rx;
  wire [31:0] Result_MEM_t;

  Comparator #(.width(4), .mode("unsigned")) comparator_1 (
    .a(OPCODE_EX), .b(4'b0011), .lt(comparator_1_lt));  // open: gt, eq
  Comparator #(.width(4), .mode("unsigned")) comparator_2 (
    .a(OPCODE_EX), .b(4'b0100), .eq(comparator_2_eq));  // open: gt, lt
  Comparator #(.width(4), .mode("unsigned")) comparator_3 (
    .a(OPCODE_EX), .b(4'b0101), .eq(comparator_3_eq));  // open: gt, lt
  Comparator #(.width(4), .mode("unsigned")) comparator_4 (
    .a(OPCODE_EX), .b(4'b0110), .eq(comparator_4_eq));  // open: gt, lt
  Comparator #(.width(4)) comparator_5 (.a(OPCODE_EX), .b(4'b1000), .eq(comparator_5_eq));  // open: gt, lt
  Comparator #(.width(4), .mode("unsigned")) comparator_6 (
    .a(OPCODE_MEM), .b(4'b0011), .lt(comparator_6_lt));  // open: gt, eq
  Comparator #(.width(4), .mode("unsigned")) comparator_7 (
    .a(OPCODE_MEM), .b(4'b0100), .eq(comparator_7_eq));  // open: gt, lt
  Comparator #(.width(4), .mode("unsigned")) comparator_8 (
    .a(OPCODE_MEM), .b(4'b0101), .eq(comparator_8_eq));  // open: gt, lt
  Comparator #(.width(4), .mode("unsigned")) comparator_9 (
    .a(OPCODE_MEM), .b(4'b0110), .eq(comparator_9_eq));  // open: gt, lt
  Comparator #(.width(4)) comparator_10 (.a(OPCODE_MEM), .b(4'b1000), .eq(comparator_10_eq));  // open: gt, lt
  Comparator #(.width(4), .mode("unsigned")) comparator_11 (
    .a(OPCODE_WB), .b(4'b0011), .lt(comparator_11_lt));  // open: gt, eq
  Comparator #(.width(4), .mode("unsigned")) comparator_12 (
    .a(OPCODE_WB), .b(4'b0100), .eq(comparator_12_eq));  // open: gt, lt
  Comparator #(.width(4), .mode("unsigned")) comparator_13 (
    .a(OPCODE_WB), .b(4'b0101), .eq(comparator_13_eq));  // open: gt, lt
  Comparator #(.width(4), .mode("unsigned")) comparator_14 (
    .a(OPCODE_WB), .b(4'b0110), .eq(comparator_14_eq));  // open: gt, lt
  Comparator #(.width(4)) comparator_15 (.a(OPCODE_WB), .b(4'b1000), .eq(comparator_15_eq));  // open: gt, lt
  Multiplexer #(.select(2), .width(32)) multiplexer_1 (
    .in0(OUT1), .in1(Result_EX), .in2(Result_MEM_t), .in3(Result_WB), .out(FOUT1), .sel(ResultSel_Ry));  // open: en
  Multiplexer #(.width(2)) multiplexer_2 (
    .in0({MEMFRy, EXRx_Ry}), .in1({WBFRy, 1'b1}), .out(ResultSel_Ry), .sel(WB_Forwad_Ry));  // open: en
  or or_1 (Possible_EX_F, comparator_1_lt, comparator_2_eq, comparator_3_eq, comparator_4_eq, comparator_5_eq);
  or or_2 (Possible_WB_F, comparator_11_lt, comparator_12_eq, comparator_13_eq, comparator_14_eq, comparator_15_eq);
  Comparator #(.width(4)) comparator_16 (.a(OPCODE_MEM), .b(4'b0101), .eq(comparator_16_eq));  // open: gt, lt
  or or_3 (Possible_MEM_F, comparator_6_lt, comparator_7_eq, comparator_8_eq, comparator_9_eq, comparator_10_eq);
  Multiplexer #(.width(32)) multiplexer_3 (
    .in0(Result_MEM), .in1(DATA_MEM), .out(Result_MEM_t), .sel(comparator_16_eq));  // open: en
  Multiplexer #(.select(2), .width(32)) multiplexer_4 (
    .in0(OUT2), .in1(Result_EX), .in2(Result_MEM_t), .in3(Result_WB), .out(FOUT2), .sel(ResultSel_Rz_Rx));  // open: en
  Comparator #(.width(4)) comparator_17 (.a(Ry_IDRR), .b(4'b0000), .eq(comparator_17_eq));  // open: gt, lt
  Comparator #(.width(4)) comparator_18 (.a(Ry_IDRR), .b(4'b0000), .eq(comparator_18_eq));  // open: gt, lt
  Comparator #(.width(4)) comparator_19 (.a(Ry_IDRR), .b(4'b0000), .eq(comparator_19_eq));  // open: gt, lt
  not not_1 (not_1_out, MEMRx_Ry);
  Multiplexer #(.width(2)) multiplexer_5 (
    .in0({MEMFRz, EXRx_Rz}), .in1({WBFRz, 1'b1}), .out(ResultSel_Rz_Rx), .sel(WB_Forwad_Rz_Rx));  // open: en
  Comparator #(.width(4)) comparator_20 (.a(EXRX), .b(Ry_IDRR), .eq(comparator_20_eq));  // open: gt, lt
  not not_2 (not_2_out, comparator_17_eq);
  Comparator #(.width(4)) comparator_21 (.a(MEMRX), .b(Ry_IDRR), .eq(comparator_21_eq));  // open: gt, lt
  not not_3 (not_3_out, comparator_18_eq);
  not not_4 (not_4_out, comparator_19_eq);
  not not_5 (not_5_out, EXRx_Ry);
  and and_1 (EXRx_Ry, comparator_20_eq, not_2_out, Possible_EX_F);
  and and_2 (MEMRx_Ry, comparator_21_eq, not_3_out, Possible_MEM_F);
  Comparator #(.width(4)) comparator_22 (.a(WBRX), .b(Ry_IDRR), .eq(comparator_22_eq));  // open: gt, lt
  and and_3 (WBRx_Ry, comparator_22_eq, not_4_out, Possible_WB_F);
  and and_4 (MEMFRy, not_5_out, MEMRx_Ry);
  and and_5 (WBFRy, not_5_out, not_1_out, WBRx_Ry);
  Comparator #(.width(4)) comparator_23 (.a(RSel_IDRR), .b(4'b0000), .eq(comparator_23_eq));  // open: gt, lt
  Comparator #(.width(4)) comparator_24 (.a(EXRX), .b(RSel_IDRR), .eq(comparator_24_eq));  // open: gt, lt
  Comparator #(.width(4)) comparator_25 (.a(RSel_IDRR), .b(4'b0000), .eq(comparator_25_eq));  // open: gt, lt
  Comparator #(.width(4)) comparator_26 (.a(MEMRX), .b(RSel_IDRR), .eq(comparator_26_eq));  // open: gt, lt
  Comparator #(.width(4)) comparator_27 (.a(RSel_IDRR), .b(4'b0000), .eq(comparator_27_eq));  // open: gt, lt
  Comparator #(.width(4)) comparator_28 (.a(WBRX), .b(RSel_IDRR), .eq(comparator_28_eq));  // open: gt, lt
  not not_6 (not_6_out, comparator_23_eq);
  not not_7 (not_7_out, EXRx_Rz);
  not not_8 (not_8_out, MEMRx_Rz);
  not not_9 (not_9_out, comparator_25_eq);
  not not_10 (not_10_out, comparator_27_eq);
  and and_6 (WBRx_Rz, comparator_28_eq, not_6_out, Possible_WB_F);
  and and_7 (MEMFRz, not_7_out, MEMRx_Rz);
  and and_8 (WBFRz, not_7_out, not_8_out, WBRx_Rz);
  and and_9 (EXRx_Rz, comparator_24_eq, not_9_out, Possible_EX_F);
  and and_10 (MEMRx_Rz, comparator_26_eq, not_10_out, Possible_MEM_F);

  // Other names for the same wires on the sheet: Result_MEM_0[31:0] = Result_MEM; Rx_EX[3:0] = EXRX;
  //   Rx_MEM[3:0] = MEMRX; Rx_WB[3:0] = WBRX
endmodule

module MEMcontrol (
  input  clk,
  input  [31:0] result_mem,
  input  [31:0] rdata2__mem,
  input  S,
  input  L,
  input  [3:0] opcode_mem,
  input  take_branch,
  output [31:0] RAM_mem,
  output [1:0] PCsel
);

  wire and_1_out, comparator_1_eq, comparator_2_eq, comparator_4_eq, comparator_5_eq, comparator_6_eq,
       or_1_out;
  wire [23:0] bit_extender_1_out;

  Comparator #(.width(4)) comparator_1 (.a(opcode_mem), .b(4'b0011), .eq(comparator_1_eq));  // open: gt, lt
  Comparator #(.width(4)) comparator_2 (.a(opcode_mem), .b(4'b1001), .eq(comparator_2_eq));  // open: gt, lt
  Bit_Extender #(.in_width(32), .out_width(24), .\type ("sign")) bit_extender_1 (
    .in(result_mem), .out(bit_extender_1_out));
  Comparator #(.width(4)) comparator_3 (.a(opcode_mem));  // open: b, gt, eq, lt
  or or_1 (or_1_out, comparator_1_eq, comparator_2_eq);
  RAM #(.addrWidth(24), .dataWidth(32), .bus("separate")) ram_1 (
    .addr(bit_extender_1_out), .din(rdata2__mem), .data(RAM_mem), .str(S), .clk(clk), .ld(L));  // open: sel, clr
  and and_1 (and_1_out, or_1_out, take_branch);
  Comparator #(.width(4)) comparator_4 (.a(opcode_mem), .b(4'b1111), .eq(comparator_4_eq));  // open: gt, lt
  Comparator #(.width(4)) comparator_5 (.a(opcode_mem), .b(4'b1111), .eq(comparator_5_eq));  // open: gt, lt
  or or_2 (PCsel[0], and_1_out, comparator_4_eq);
  Comparator #(.width(4)) comparator_6 (.a(opcode_mem), .b(4'b0100), .eq(comparator_6_eq));  // open: gt, lt
  or or_3 (PCsel[1], comparator_6_eq, comparator_5_eq);

  // Other names for the same wires on the sheet: LDMEM_MEM = L
endmodule

module NENEW (
  input  [3:0] ID_RR_OPCODE,
  input  [31:0] IDRR_out1,
  input  [3:0] IDRR_Ry,
  input  [3:0] IDRR_Rz,
  input  [31:0] IDRR_out2,
  input  [3:0] EX_OPCODE,
  input  [3:0] EX_Rx,
  input  [31:0] EX_Result,
  input  [3:0] MEM_OPCODE,
  input  [3:0] MEM_Rx,
  input  [31:0] MEM_Res,
  input  [31:0] RAM_Result,
  input  [3:0] WB_OPCODE,
  input  [3:0] WB_Rx,
  input  [31:0] WB_Result,
  output [31:0] Ry,
  output [31:0] Rz
);

  wire _0, _0__Ry, _1, _1__Ry, _2__Ry, _2__Rz, _3__Ry, _3__Rz, comparator_1_eq, comparator_2_eq,
       comparator_3_lt, comparator_4_eq, comparator_5_eq, comparator_6_eq, comparator_7_eq, comparator_8_lt,
       comparator_9_eq, comparator_10_eq, comparator_11_eq, comparator_12_eq, comparator_13_lt,
       comparator_14_eq, comparator_15_eq, comparator_16_eq, comparator_17_eq, ENABLE_EX, ENABLE_MEM,
       ENABLE_WB, EX__ForwardRy, EX__ForwardRz, MEM__ForwardRy, MEM__ForwardRz, or_1_out, Ry_FORWARD_EX_Rx,
       Ry_FORWARD_MEM_Rx, Ry_FORWARD_WB_Rx, Ry_MEM_FORWARD, Rz_FORWARD_EX_Rx, Rz_FORWARD_MEM_Rx,
       Rz_FORWARD_WB_Rx, Rz_MEM_FORWARD, WB__ForwardRy, WB__ForwardRz;
  wire [1:0] Ry_t, Rz_t;
  wire [31:0] MEM_Result;

  Comparator #(.width(4)) comparator_1 (.a(MEM_OPCODE), .b(4'b0101), .eq(comparator_1_eq));  // open: gt, lt
  Comparator #(.width(4)) comparator_2 (.a(MEM_OPCODE), .b(4'b0110), .eq(comparator_2_eq));  // open: gt, lt
  or or_1 (or_1_out, comparator_1_eq, comparator_2_eq);
  Multiplexer #(.width(32), .enable("false")) multiplexer_1 (
    .in0(MEM_Res), .in1(RAM_Result), .out(MEM_Result), .sel(or_1_out));
  Comparator #(.width(4)) comparator_3 (.a(WB_OPCODE), .b(4'b0011), .lt(comparator_3_lt));  // open: gt, eq
  Comparator #(.width(4)) comparator_4 (.a(WB_OPCODE), .b(4'b0100), .eq(comparator_4_eq));  // open: gt, lt
  Comparator #(.width(4)) comparator_5 (.a(WB_OPCODE), .b(4'b0101), .eq(comparator_5_eq));  // open: gt, lt
  Comparator #(.width(4)) comparator_6 (.a(WB_OPCODE), .b(4'b0110), .eq(comparator_6_eq));  // open: gt, lt
  Comparator #(.width(4)) comparator_7 (.a(WB_OPCODE), .b(4'b1000), .eq(comparator_7_eq));  // open: gt, lt
  Comparator #(.width(4)) comparator_8 (.a(EX_OPCODE), .b(4'b0011), .lt(comparator_8_lt));  // open: gt, eq
  Comparator #(.width(4)) comparator_9 (.a(EX_OPCODE), .b(4'b0100), .eq(comparator_9_eq));  // open: gt, lt
  Comparator #(.width(4)) comparator_10 (.a(EX_OPCODE), .b(4'b0101), .eq(comparator_10_eq));  // open: gt, lt
  Comparator #(.width(4)) comparator_11 (.a(EX_OPCODE), .b(4'b0110), .eq(comparator_11_eq));  // open: gt, lt
  Comparator #(.width(4)) comparator_12 (.a(EX_OPCODE), .b(4'b1000), .eq(comparator_12_eq));  // open: gt, lt
  Comparator #(.width(4)) comparator_13 (.a(MEM_OPCODE), .b(4'b0011), .lt(comparator_13_lt));  // open: gt, eq
  Comparator #(.width(4)) comparator_14 (.a(MEM_OPCODE), .b(4'b0100), .eq(comparator_14_eq));  // open: gt, lt
  Comparator #(.width(4)) comparator_15 (.a(MEM_OPCODE), .b(4'b0101), .eq(comparator_15_eq));  // open: gt, lt
  Comparator #(.width(4)) comparator_16 (.a(MEM_OPCODE), .b(4'b0110), .eq(comparator_16_eq));  // open: gt, lt
  Comparator #(.width(4)) comparator_17 (.a(MEM_OPCODE), .b(4'b1000), .eq(comparator_17_eq));  // open: gt, lt
  or or_2 (ENABLE_WB, comparator_3_lt, comparator_4_eq, comparator_5_eq, comparator_6_eq, comparator_7_eq);
  or or_3 (ENABLE_EX, comparator_8_lt, comparator_9_eq, comparator_10_eq, comparator_11_eq, comparator_12_eq);
  Comparator #(.width(4)) comparator_18 (.a(IDRR_Ry), .b(EX_Rx), .eq(EX__ForwardRy));  // open: gt, lt
  Comparator #(.width(4)) comparator_19 (.a(IDRR_Rz), .b(EX_Rx), .eq(EX__ForwardRz));  // open: gt, lt
  Comparator #(.width(4)) comparator_20 (.a(IDRR_Ry), .b(MEM_Rx), .eq(MEM__ForwardRy));  // open: gt, lt
  Comparator #(.width(4)) comparator_21 (.a(IDRR_Rz), .b(MEM_Rx), .eq(MEM__ForwardRz));  // open: gt, lt
  or or_4 (ENABLE_MEM, comparator_13_lt, comparator_14_eq, comparator_15_eq, comparator_16_eq, comparator_17_eq);
  Comparator #(.width(4)) comparator_22 (.a(IDRR_Ry), .b(WB_Rx), .eq(WB__ForwardRy));  // open: gt, lt
  Comparator #(.width(4)) comparator_23 (.a(IDRR_Rz), .b(WB_Rx), .eq(WB__ForwardRz));  // open: gt, lt
  and and_1 (Ry_FORWARD_EX_Rx, ENABLE_EX, EX__ForwardRy);
  and and_2 (Rz_FORWARD_EX_Rx, ENABLE_EX, EX__ForwardRz);
  and and_3 (Rz_FORWARD_MEM_Rx, ENABLE_MEM, MEM__ForwardRz);
  and and_4 (Ry_FORWARD_MEM_Rx, ENABLE_MEM, MEM__ForwardRy);
  and and_5 (Ry_FORWARD_WB_Rx, ENABLE_EX, WB__ForwardRy);
  and and_6 (Rz_FORWARD_WB_Rx, ENABLE_EX, WB__ForwardRz);
  Multiplexer #(.select(2), .width(32), .enable("false")) multiplexer_2 (
    .in0(IDRR_out1), .in1(EX_Result), .in2(MEM_Result), .in3(WB_Result), .out(Ry), .sel(Ry_t));
  Multiplexer #(.select(2), .width(32), .enable("false")) multiplexer_3 (
    .in0(IDRR_out2), .in1(EX_Result), .in2(MEM_Result), .in3(WB_Result), .out(Rz), .sel(Rz_t));
  Comparator #(.width(3)) comparator_24 (
    .a({Ry_FORWARD_EX_Rx, Ry_FORWARD_MEM_Rx, Ry_FORWARD_WB_Rx}), .b(3'b000), .eq(_0__Ry));  // open: gt, lt
  Comparator #(.width(3)) comparator_25 (
    .a({Ry_FORWARD_EX_Rx, Ry_FORWARD_MEM_Rx, Ry_FORWARD_WB_Rx}), .b(3'b001), .eq(_1__Ry));  // open: gt, lt
  Comparator #(.width(3)) comparator_26 (
    .a({Ry_FORWARD_EX_Rx, Ry_FORWARD_MEM_Rx, Ry_FORWARD_WB_Rx}), .b(3'b010), .eq(_2__Ry));  // open: gt, lt
  Comparator #(.width(3)) comparator_27 (
    .a({Ry_FORWARD_EX_Rx, Ry_FORWARD_MEM_Rx, Ry_FORWARD_WB_Rx}), .b(3'b011), .eq(_3__Ry));  // open: gt, lt
  Comparator #(.width(3)) comparator_28 (
    .a({Rz_FORWARD_EX_Rx, Rz_FORWARD_MEM_Rx, Rz_FORWARD_WB_Rx}), .b(3'b000), .eq(_0));  // open: gt, lt
  Comparator #(.width(3)) comparator_29 (
    .a({Rz_FORWARD_EX_Rx, Rz_FORWARD_MEM_Rx, Rz_FORWARD_WB_Rx}), .b(3'b001), .eq(_1));  // open: gt, lt
  Comparator #(.width(3)) comparator_30 (
    .a({Rz_FORWARD_EX_Rx, Rz_FORWARD_MEM_Rx, Rz_FORWARD_WB_Rx}), .b(3'b010), .eq(_2__Rz));  // open: gt, lt
  Comparator #(.width(3)) comparator_31 (
    .a({Rz_FORWARD_EX_Rx, Rz_FORWARD_MEM_Rx, Rz_FORWARD_WB_Rx}), .b(3'b011), .eq(_3__Rz));  // open: gt, lt
  assign Ry_t = _0__Ry ? 2'b00 : 2'bz;  // Controlled_Buffer controlled_buffer_1
  assign Ry_t = Ry_FORWARD_EX_Rx ? 2'b01 : 2'bz;  // Controlled_Buffer controlled_buffer_2
  assign Ry_t = Ry_MEM_FORWARD ? 2'b10 : 2'bz;  // Controlled_Buffer controlled_buffer_3
  assign Ry_t = _1__Ry ? 2'b11 : 2'bz;  // Controlled_Buffer controlled_buffer_4
  or or_5 (Ry_MEM_FORWARD, _2__Ry, _3__Ry);
  assign Rz_t = _0 ? 2'b00 : 2'bz;  // Controlled_Buffer controlled_buffer_5
  assign Rz_t = Rz_FORWARD_EX_Rx ? 2'b01 : 2'bz;  // Controlled_Buffer controlled_buffer_6
  assign Rz_t = Rz_MEM_FORWARD ? 2'b10 : 2'bz;  // Controlled_Buffer controlled_buffer_7
  assign Rz_t = _1 ? 2'b11 : 2'bz;  // Controlled_Buffer controlled_buffer_8
  or or_6 (Rz_MEM_FORWARD, _2__Rz, _3__Rz);

  // Other names for the same wires on the sheet: IDDR_Rout1[31:0] = IDRR_out1; IDDR_Rout2[31:0] = IDRR_out2;
  //   IDDR_Ry[3:0] = IDRR_Ry; IDDR_Rz[3:0] = IDRR_Rz
endmodule
